# Fritzing sketch CameraShowSchematic (saved by Fritzing 0.7.12b)
breadboards: 1

parts:
  U3 = attiny85 [package=dip]
  U4 = 74HC595 [package="DIP16 [THT]"]
  LED1 = LED - 5mm [color="Blue (470nm)" package="5 mm [THT]"]
  LED2 = LED - 5mm [color="Blue (470nm)" package="5 mm [THT]"]
  LED3 = LED - 5mm [color="Blue (470nm)" package="5 mm [THT]"]
  LED4 = LED - 5mm [color="Blue (470nm)" package="5 mm [THT]"]
  LED5 = LED - 5mm [color="Blue (470nm)" package="5 mm [THT]"]
  LED6 = LED - 5mm [color="Blue (470nm)" package="5 mm [THT]"]
  LED7 = LED - 5mm [color="Blue (470nm)" package="5 mm [THT]"]
  LED8 = LED - 5mm [color="Blue (470nm)" package="5 mm [THT]"]
  VCC1 = Battery
  C1 = Electrolytic Capacitor [capacitance=1µF package="100 mil [THT, electrolytic]"]
  U5 = attiny85 [package=dip]
  LED9 = LED - 5mm [color="Blue (470nm)" package="5 mm [THT]"]
  LED10 = LED - 5mm [color="Blue (470nm)" package="5 mm [THT]"]
  LED11 = LED - 5mm [color="Blue (470nm)" package="5 mm [THT]"]
  LED12 = LED - 5mm [color="Blue (470nm)" package="5 mm [THT]"]
  LED13 = LED - 5mm [color="Blue (470nm)" package="5 mm [THT]"]
  LED14 = LED - 5mm [color="Blue (470nm)" package="5 mm [THT]"]
  LED15 = LED - 5mm [color="Blue (470nm)" package="5 mm [THT]"]
  LED16 = LED - 5mm [color="Blue (470nm)" package="5 mm [THT]"]
  U6 = 74HC595 [package="DIP16 [THT]"]
  VCC2 = Battery
  C2 = Electrolytic Capacitor [capacitance=1µF package="100 mil [THT, electrolytic]"]

nets:
  N1: U3.Pin_4, U4.GND, U4.OE, LED1.cathode, LED2.cathode, LED3.cathode, LED4.cathode, LED5.cathode, LED6.cathode, LED7.cathode, LED8.cathode, VCC1.-, C1.-
  N2: U3.Pin_5, U4.DS
  N3: U3.Pin_6, U4.ST_CP
  N4: U3.Pin_7, U4.SH_CP
  N5: U3.Pin_8, U4.MR, U4.VCC, VCC1.+, C1.+
  N6: U4.Q1, LED1.anode
  N7: U4.Q2, LED3.anode
  N8: U4.Q3, LED4.anode
  N9: U4.Q4, LED2.anode
  N10: U4.Q5, LED8.anode
  N11: U4.Q6, LED7.anode
  N12: U4.Q7, LED6.anode
  N13: U4.Q0, LED5.anode
  N14: U5.Pin_4, LED9.cathode, LED10.cathode, LED11.cathode, LED12.cathode, LED13.cathode, LED14.cathode, LED15.cathode, LED16.cathode, U6.GND, U6.OE, VCC2.-, C2.-
  N15: U5.Pin_6, U6.ST_CP
  N16: U5.Pin_7, U6.SH_CP
  N17: U5.Pin_8, U6.MR, U6.VCC, VCC2.+, C2.+
  N18: LED9.anode, U6.Q5
  N19: LED10.anode, U6.Q6
  N20: LED11.anode, U6.Q7
  N21: LED12.anode, U6.Q0
  N22: LED13.anode, U6.Q3
  N23: LED14.anode, U6.Q2
  N24: LED15.anode, U6.Q4
  N25: LED16.anode, U6.Q1
